# Fritzing sketch esquematico-exemplos-02-03-04 (saved by Fritzing 0.9.3b)
breadboards: 1

parts:
  Componente1 = Arduino Uno (Rev3)
  R1 = Resistor [tolerance=±5% resistance=220 package=THT]
  LED1 = smd LED [color="Red (633nm)" package="0603 [SMD]"]

nets:
  N1: Componente1.D13/SCK, R1.Pin_0
  N2: Componente1.GND, LED1.cathode
  N3: R1.Pin_1, LED1.anode
