# Fritzing sketch esquematico-exemplos-06-07-08 (saved by Fritzing 0.9.3b)
breadboards: 1

parts:
  Componente1 = Arduino Uno (Rev3)
  R2 = Resistor [tolerance=±5% resistance=220 package=THT]
  LDR = Photocell (LDR) [package=THT]

nets:
  N1: Componente1.A0, R2.Pin_0, LDR.pin_0
  N2: Componente1.GND, R2.Pin_1
  N3: Componente1.5V, LDR.pin_1
