# Fritzing sketch esquematico-exemplos-10-11 (saved by Fritzing 0.9.1b)
breadboards: 1

parts:
  LED1 = smd LED [color="Red (633nm)" package="0603 [SMD]"]
  R1 = Resistor [tolerance=±5% resistance=220 package=THT]
  Componente1 = Arduino Uno (Rev3)
  R2 = Resistor [tolerance=±5% resistance=220 package=THT]
  LDR = Photocell (LDR) [package=THT]

nets:
  N1: LED1.cathode, Componente1.GND, R2.Pin_1
  N2: LED1.anode, R1.Pin_1
  N3: R1.Pin_0, Componente1.D13/SCK
  N4: Componente1.A0, R2.Pin_0, LDR.pin_0
  N5: Componente1.5V, LDR.pin_1
